# Fritzing sketch ShiftRegister (saved by Fritzing 0.9.4)
breadboards: 2

parts:
  Part1 = Arduino Uno (Rev3)
  IC1 = SHIFT REGISTER [package=dil16]
  LED1 = smd LED [color="Red (633nm)" package="0603 [SMD]"]
  LED2 = smd LED [color="Red (633nm)" package="0603 [SMD]"]
  R1 = Resistor [tolerance=±5% resistance=220 package="0805 [SMD]"]
  LED3 = smd LED [color="Red (633nm)" package="0603 [SMD]"]
  LED4 = smd LED [color="Red (633nm)" package="0603 [SMD]"]
  LED5 = smd LED [color="Red (633nm)" package="0603 [SMD]"]
  LED6 = smd LED [color="Red (633nm)" package="0603 [SMD]"]
  LED7 = smd LED [color="Red (633nm)" package="0603 [SMD]"]
  LED8 = smd LED [color="Red (633nm)" package="0603 [SMD]"]
  R2 = Resistor [tolerance=±5% resistance=220 package="0805 [SMD]"]
  R3 = Resistor [tolerance=±5% resistance=220 package="0805 [SMD]"]
  R4 = Resistor [tolerance=±5% resistance=220 package="0805 [SMD]"]
  R5 = Resistor [tolerance=±5% resistance=220 package="0805 [SMD]"]
  R6 = Resistor [tolerance=±5% resistance=220 package="0805 [SMD]"]
  R7 = Resistor [tolerance=±5% resistance=220 package="0805 [SMD]"]
  R8 = Resistor [tolerance=±5% resistance=220 package="0805 [SMD]"]

nets:
  N1: Part1.D2, IC1.SER
  N2: Part1.D3_PWM, IC1.SCK
  N3: Part1.D4, IC1.RCK
  5V: Part1.5V, IC1.SCL, IC1.VCC
  GND: Part1.GND, IC1.GND, IC1.G, LED1.cathode, LED2.cathode, LED3.cathode, LED4.cathode, LED5.cathode, LED6.cathode, LED7.cathode, LED8.cathode
  N4: IC1.QB, R2.Pin_1
  N5: IC1.QC, R3.Pin_1
  N6: IC1.QD, R4.Pin_1
  N7: IC1.QE, R5.Pin_1
  N8: IC1.QF, R6.Pin_1
  N9: IC1.QG, R7.Pin_1
  N10: IC1.QH, R8.Pin_1
  N11: LED1.anode, R1.Pin_0
  N12: LED2.anode, R2.Pin_0
  N13: LED3.anode, R3.Pin_0
  N14: LED4.anode, R8.Pin_0
  N15: LED5.anode, R7.Pin_0
  N16: LED6.anode, R6.Pin_0
  N17: LED7.anode, R5.Pin_0
  N18: LED8.anode, R4.Pin_0
